// Logisim project ArquitecturaCombinacional.circ as structural Verilog: 9 circuits, main circuit main
module main (
  input  in_1,
  input  in_2,
  input  in_3,
  input  in_4,
  input  in_5,
  input  in_6,
  output out_7,
  output out_8,
  output out_9
);

  and and_1 (out_7, in_1, in_3);
  or or_1 (out_9, in_5, in_6);
  xor xor_1 (out_8, in_2, in_4);
  // NOT_Gate not_1 is placed but not wired

  // Notes on the sheet:
  //   AND
  //   OR
  //   XOR   O     OR-EXCLUYENTE
  //   NEGACION
endmodule

module Semisumador (
  input  X,
  input  Y,
  output s,
  output ac
);

  and and_1 (ac, X, Y);
  xor xor_1 (s, X, Y);

  // Notes on the sheet:
  //   Un semisumador es el circuito que representa la suma entre 2 bits
  //   ac
  //   x
  //   +
  //   y
  //   __
  //   S
endmodule

module Sumador_Total_Base (
  input  Ac_I,
  input  X,
  input  Y,
  output S,
  output Ac_O
);

  wire semisumador_1_ac, semisumador_1_s, semisumador_2_ac;

  Semisumador semisumador_1 (.X(Ac_I), .Y(X), .s(semisumador_1_s), .ac(semisumador_1_ac));
  Semisumador semisumador_2 (.X(semisumador_1_s), .Y(Y), .s(S), .ac(semisumador_2_ac));
  or or_1 (Ac_O, semisumador_2_ac, semisumador_1_ac);

  // Notes on the sheet:
  //   ac out
  //   ac in
  //   y
  //   z
  //   __
  //   s
  //   Sumador de 2 bits con posible acarreo entrante
  //   Esta es la forma que vamos a adotpar para construir nuestros circuitos, es el modulo que siempre se repite
  //   S1
endmodule

module Suma_de_dos_numeros_de_dos_bits (
  input  a0,
  input  b0,
  input  a1,
  input  b1,
  output S1,
  output S2,
  output AC
);

  wire semisumador_1_ac, semisumador_2_ac, semisumador_2_s, semisumador_3_ac;

  Semisumador semisumador_1 (.X(a0), .Y(b0), .s(S1), .ac(semisumador_1_ac));
  Semisumador semisumador_2 (.X(a1), .Y(semisumador_1_ac), .s(semisumador_2_s), .ac(semisumador_2_ac));
  Semisumador semisumador_3 (.X(semisumador_2_s), .Y(b1), .s(S2), .ac(semisumador_3_ac));
  or or_1 (AC, semisumador_3_ac, semisumador_2_ac);

  // Notes on the sheet:
  //   Ahora tenenmos que sumar dos digitos de dos bits
  //   AC
  //   a1 a0
  //   b1  b0
  //   ____
  //   S1 S2
endmodule

module Sumador_Con_Base (
  input  b1,
  input  a1,
  input  b0,
  input  a0,
  input  in_5,
  output out_6,
  output S2,
  output out_8,
  output S1
);

  Sumador_Total_Base sumador_total_base_1 (.Ac_I(out_8), .X(a1), .Y(b1), .S(S2), .Ac_O(out_6));
  Sumador_Total_Base sumador_total_base_2 (.Ac_I(in_5), .X(a0), .Y(b0), .S(S1), .Ac_O(out_8));

  // Notes on the sheet:
  //   AC
  //   a1 a0
  //   b1  b0
  //   ____
  //   S1 S2
  //   AC in = 0
  //   Esta es la forma en la que se construyen los sumadores que vamos a utilizar a lo largo de la materia
endmodule

module RESTA_Complemento_a_Dos (
  input  b2,
  input  b1,
  input  b0,
  input  a2,
  input  a1,
  input  a0,
  input  in_7,
  output BIT_SIGNO,
  output out_9,
  output out_10,
  output out_11
);

  wire not_1_out, not_2_out, not_3_out, not_4_out, sumador_total_base_1_s, sumador_total_base_2_s,
       sumador_total_base_3_ac_o, sumador_total_base_3_s, sumador_total_base_4_ac_o, sumador_total_base_4_s,
       sumador_total_base_5_ac_o, sumador_total_base_5_s, sumador_total_base_6_ac_o, sumador_total_base_6_s;

  not not_1 (not_1_out, BIT_SIGNO);
  not not_2 (not_2_out, b2);
  Sumador_Total_Base sumador_total_base_1 (
    .Ac_I(sumador_total_base_3_ac_o), .X(a2), .Y(not_2_out), .S(sumador_total_base_1_s), .Ac_O(BIT_SIGNO));
  Sumador_Total_Base sumador_total_base_2 (
    .Ac_I(sumador_total_base_4_ac_o), .X(not_1_out), .Y(sumador_total_base_1_s), .S(sumador_total_base_2_s));  // open: Ac_O
  xor xor_1 (out_9, not_1_out, sumador_total_base_2_s);
  not not_3 (not_3_out, b1);
  Sumador_Total_Base sumador_total_base_3 (
    .Ac_I(sumador_total_base_5_ac_o), .X(a1), .Y(not_3_out), .S(sumador_total_base_3_s),
    .Ac_O(sumador_total_base_3_ac_o));
  Sumador_Total_Base sumador_total_base_4 (
    .Ac_I(sumador_total_base_6_ac_o), .X(not_1_out), .Y(sumador_total_base_3_s), .S(sumador_total_base_4_s),
    .Ac_O(sumador_total_base_4_ac_o));
  xor xor_2 (out_10, not_1_out, sumador_total_base_4_s);
  not not_4 (not_4_out, b0);
  Sumador_Total_Base sumador_total_base_5 (
    .Ac_I(in_7), .X(a0), .Y(not_4_out), .S(sumador_total_base_5_s), .Ac_O(sumador_total_base_5_ac_o));
  Sumador_Total_Base sumador_total_base_6 (
    .Ac_I(not_1_out), .X(1'b0), .Y(sumador_total_base_5_s), .S(sumador_total_base_6_s),
    .Ac_O(sumador_total_base_6_ac_o));
  xor xor_3 (out_11, not_1_out, sumador_total_base_6_s);

  // Notes on the sheet:
  //   Supongamos que tengo la suma de dos numeros A y B de 3 bits en Complemento a 2 y quiero hacer la resta A-B.
  //   Para esto vamos a tener que primero complementara B y sumarle 1. Por eso tambien adoptamos esta estructura como sumador base, la suma del inicio nos ayuda y nos queda mas comodo para operaciones que vamos a ver
  //   1 constante
endmodule

module Sumador_Restador (
  input  b2,
  input  a2,
  input  b1,
  input  a1,
  input  b0,
  input  a0,
  input  in_7,
  output out_8,
  output S3,
  output S2,
  output S1
);

  wire sumador_total_base_2_ac_o, sumador_total_base_3_ac_o, xor_1_out, xor_2_out, xor_3_out;

  xor xor_1 (xor_1_out, in_7, b2);
  Sumador_Total_Base sumador_total_base_1 (
    .Ac_I(sumador_total_base_2_ac_o), .X(a2), .Y(xor_1_out), .S(S3), .Ac_O(out_8));
  xor xor_2 (xor_2_out, in_7, b1);
  Sumador_Total_Base sumador_total_base_2 (
    .Ac_I(sumador_total_base_3_ac_o), .X(a1), .Y(xor_2_out), .S(S2), .Ac_O(sumador_total_base_2_ac_o));
  xor xor_3 (xor_3_out, in_7, b0);
  Sumador_Total_Base sumador_total_base_3 (
    .Ac_I(in_7), .X(a0), .Y(xor_3_out), .S(S1), .Ac_O(sumador_total_base_3_ac_o));

  // Notes on the sheet:
  //   0 si es suma o 1 si es resta
endmodule

module Comparador_Suma (
  input  in_1,
  input  in_2,
  input  in_3,
  input  in_4,
  input  in_5,
  input  in_6,
  output A_mayor_B,
  output A_Igual_B,
  output A_menor_B
);

  wire and_1_out, not_1_out, sumador_total_base_1_ac_o, sumador_total_base_1_s, sumador_total_base_2_ac_o,
       sumador_total_base_2_s, sumador_total_base_3_ac_o, sumador_total_base_3_s, xor_1_out, xor_2_out,
       xor_3_out;

  xor xor_1 (xor_1_out, 1'b1, in_1);
  Sumador_Total_Base sumador_total_base_1 (
    .Ac_I(sumador_total_base_2_ac_o), .X(in_2), .Y(xor_1_out), .S(sumador_total_base_1_s),
    .Ac_O(sumador_total_base_1_ac_o));
  and and_1 (and_1_out, ~sumador_total_base_1_s, ~sumador_total_base_2_s, ~sumador_total_base_3_s);  // AND_Gate
  not not_1 (not_1_out, and_1_out);
  and and_2 (A_mayor_B, sumador_total_base_1_ac_o, not_1_out);
  xor xor_2 (xor_2_out, 1'b1, in_3);
  and and_3 (A_menor_B, A_mayor_B, A_Igual_B);
  Sumador_Total_Base sumador_total_base_2 (
    .Ac_I(sumador_total_base_3_ac_o), .X(in_4), .Y(xor_2_out), .S(sumador_total_base_2_s),
    .Ac_O(sumador_total_base_2_ac_o));
  and and_4 (A_Igual_B, sumador_total_base_1_ac_o, ~sumador_total_base_1_s, ~sumador_total_base_2_s, ~sumador_total_base_3_s);  // AND_Gate
  xor xor_3 (xor_3_out, 1'b1, in_5);
  Sumador_Total_Base sumador_total_base_3 (
    .Ac_I(1'b1), .X(in_6), .Y(xor_3_out), .S(sumador_total_base_3_s), .Ac_O(sumador_total_base_3_ac_o));

  // Notes on the sheet:
  //   Acarreo
endmodule

module Comparador_Metodo_3 (
  input  in_1,
  input  in_2,
  input  in_3,
  input  in_4,
  input  in_5,
  input  in_6,
  output A_mayor_B,
  output A_menor_B,
  output A_Igual_B
);

  wire and_1_out, and_2_out, and_3_out, and_4_out, and_5_out, xnor_1_out, xnor_2_out, xnor_3_out, xnor_4_out,
       xnor_5_out, xnor_6_out;

  and and_1 (and_1_out, in_1, ~in_4);  // AND_Gate
  and and_2 (and_2_out, in_2, ~in_5);  // AND_Gate
  and and_3 (and_3_out, in_3, ~in_6);  // AND_Gate
  xnor xnor_1 (xnor_1_out, in_1, in_4);
  xnor xnor_2 (xnor_2_out, in_2, in_5);
  xnor xnor_3 (xnor_3_out, in_6, in_3);
  xnor xnor_4 (xnor_4_out, in_1, in_4);
  xnor xnor_5 (xnor_5_out, in_1, in_4);
  xnor xnor_6 (xnor_6_out, in_2, in_5);
  and and_4 (and_4_out, xnor_4_out, and_2_out);
  and and_5 (and_5_out, xnor_5_out, xnor_6_out, and_3_out);
  and and_6 (A_Igual_B, xnor_1_out, xnor_2_out, xnor_3_out);
  or or_1 (A_mayor_B, and_1_out, and_4_out, and_5_out);
  and and_7 (A_menor_B, ~A_mayor_B, ~A_Igual_B);  // AND_Gate
endmodule
